# Fritzing sketch fritzing-schema (saved by Fritzing 0.9.3b)
breadboards: 1

parts:
  Componente1 = Arduino Micro (Rev3)  # not connected
  S1 = Pushbutton [package="[THT]"]
  R1 = Resistor [tolerance=±5% resistance=10k package=THT]
  S2 = Pushbutton [package="[THT]"]
  R2 = Resistor [tolerance=±5% resistance=10k package=THT]
  S3 = Pushbutton [package="[THT]"]
  S4 = Pushbutton [package="[THT]"]
  R3 = Resistor [tolerance=±5% resistance=10k package=THT]
  R4 = Resistor [tolerance=±5% resistance=10k package=THT]
  LED1 = LED - 5mm [color="Blue (470nm)" package="5 mm [THT]"]
  R5 = Resistor [tolerance=±5% resistance=220 package=THT]
  LED2 = LED - 5mm [color="Red (633nm)" package="5 mm [THT]"]
  R6 = Resistor [tolerance=±5% resistance=220 package=THT]
  R7 = Resistor [tolerance=±5% resistance=220 package=THT]
  LED3 = LED - 5mm [color="Yellow (585nm)" package="5 mm [THT]"]
  R8 = Resistor [tolerance=±5% resistance=220 package=THT]
  LED4 = LED - 5mm [color="Green (565nm)" package="5 mm [THT]"]
  LCD1 = LCD screen
  LCM1602_IIC2 = LCM1602 IIC [part_number="LCM1602 IIC" chip_label="LCM1602 IIC" package="DIP (Dual Inline) [THT]"]

nets:
  N1: S1.Pin_1, S1.Pin_2, S2.Pin_1, S2.Pin_2, S3.Pin_1, S3.Pin_2, S4.Pin_1, S4.Pin_2, R5.Pin_0, R6.Pin_0, R7.Pin_0, R8.Pin_0
  N2: S1.Pin_3, S1.Pin_4, R1.Pin_0
  N3: R1.Pin_1, R2.Pin_1, R3.Pin_1, R4.Pin_1, LCM1602_IIC2.GND
  N4: S2.Pin_3, S2.Pin_4, R2.Pin_0
  N5: S3.Pin_3, S3.Pin_4, R3.Pin_0
  N6: S4.Pin_3, S4.Pin_4, R4.Pin_0
  N7: LED1.cathode, R5.Pin_1
  N8: LED2.cathode, R6.Pin_1
  N9: R7.Pin_1, LED3.cathode
  N10: R8.Pin_1, LED4.cathode
  VSS: LCD1.VSS, LCM1602_IIC2.VSS
  VDD: LCD1.VDD, LCM1602_IIC2.VDD
  N11: LCD1.V0, LCM1602_IIC2.V0
  N12: LCD1.RS, LCM1602_IIC2.RS
  N13: LCD1.R/W, LCM1602_IIC2.RW
  N14: LCD1.E, LCM1602_IIC2.E
  N15: LCD1.DB0, LCM1602_IIC2.D0
  N16: LCD1.DB1, LCM1602_IIC2.D1
  N17: LCD1.DB2, LCM1602_IIC2.D2
  N18: LCD1.DB3, LCM1602_IIC2.D3
  N19: LCD1.DB4, LCM1602_IIC2.D4
  N20: LCD1.DB5, LCM1602_IIC2.D5
  N21: LCD1.DB6, LCM1602_IIC2.D6
  N22: LCD1.DB7, LCM1602_IIC2.D7
  N23: LCD1.LED+, LCM1602_IIC2.A
  N24: LCD1.LED-, LCM1602_IIC2.K

custom parts:
  LCM1602 IIC: I2C-Module to use a 1602 or 2004 LCD on with the wire.h libory Serial LCD Modul
